# Fritzing sketch breadboard_layout (saved by Fritzing 0.9.4)
circuit board: 8.46667cm x 5.64444cm
breadboards: 1

parts:
  U1 = NodeMCU V1.0
  R1 = Resistor [tolerance=±5% resistance=330 package=THT]
  LED1 = LED - 3mm [color="Red (633nm)" package="3 mm [THT]"]
  LED2 = LED - 3mm [color="Yellow (574nm)" package="3 mm [THT]"]
  LED3 = LED - 3mm [color="Green (555nm)" package="3 mm [THT]"]
  R2 = Resistor [tolerance=±5% resistance=330 package=THT]
  R3 = Resistor [tolerance=±5% resistance=330 package=THT]
  R4 = Trimmer Potentiometer [maximum_resistance=10kΩ package=THT]

nets:
  N1: U1.D1, R3.Pin_0
  N2: U1.3V3, R4.leg1
  N3: U1.GND, R4.leg2
  N4: U1.D5, R2.Pin_0
  N5: U1.D6, R1.Pin_0
  N6: U1.A0, R4.wiper
  N7: R1.Pin_1, LED1.anode
  N8: LED2.anode, R2.Pin_1
  N9: LED3.anode, R3.Pin_1

notes:
  The 10K trimmer
  is emulating an
  analog sensor.

custom parts:
  NodeMCU V1.0: ESP8266 based NodeMCU
